// Logisim project alu.circ as structural Verilog: 1 circuit, main circuit main
module main (
  input  [31:0] X,
  input  [31:0] Y,
  input  [3:0] Switch,
  output Signed_Overflow,
  output Equal,
  output [31:0] Result
);

  wire and_2_out, and_3_out, and_4_out, and_5_out, and_6_out, comparator_1_lt, comparator_2_lt,
       comparator_4_eq, comparator_5_eq, comparator_6_eq, comparator_7_eq, not_1_out, not_2_out, not_3_out,
       not_4_out, not_5_out, or_2_out, or_3_out, xnor_1_out, xor_1_out;
  wire [4:0] bit_extender_1_out, bit_extender_2_out, bit_extender_3_out;
  wire [31:0] _0_sll, _1_srl, _2_sra, _5_add, _6_addu, _7_sub, _8_subu, _9_and, _10_or, _11_slt, _12_sltu;

  Bit_Extender #(.in_width(32), .out_width(5)) bit_extender_1 (.in(X), .out(bit_extender_1_out));
  Bit_Extender #(.in_width(32), .out_width(5)) bit_extender_2 (.in(X), .out(bit_extender_2_out));
  Shifter #(.width(32), .shift("ar")) shifter_1 (.in(Y), .\dist (bit_extender_3_out), .out(_2_sra));
  Bit_Extender #(.in_width(32), .out_width(5)) bit_extender_3 (.in(X), .out(bit_extender_3_out));
  Subtractor #(.width(32)) subtractor_1 (.a(X), .b(Y), .out(_8_subu));  // open: bin, bout
  assign _9_and = X & Y;  // AND_Gate and_1, 32 bits wide
  assign _10_or = X | Y;  // OR_Gate or_1, 32 bits wide
  Comparator #(.width(32)) comparator_1 (.a(X), .b(Y), .lt(comparator_1_lt));  // open: gt, eq
  Comparator #(.width(32), .mode("unsigned")) comparator_2 (.a(X), .b(Y), .lt(comparator_2_lt));  // open: gt, eq
  Comparator #(.width(32), .mode("unsigned")) comparator_3 (.a(X), .b(Y), .eq(Equal));  // open: gt, lt
  Shifter #(.width(32)) shifter_2 (.in(Y), .\dist (bit_extender_1_out), .out(_0_sll));
  Shifter #(.width(32), .shift("lr")) shifter_3 (.in(Y), .\dist (bit_extender_2_out), .out(_1_srl));
  assign _11_slt = {{31{1'b0}}, comparator_1_lt};  // Bit_Extender bit_extender_4
  assign _12_sltu = {{31{1'b0}}, comparator_2_lt};  // Bit_Extender bit_extender_5
  Adder #(.width(32)) adder_1 (.a(Y), .b(X), .out(_6_addu));  // open: cin, cout
  Adder #(.width(32)) adder_2 (.a(X), .b(Y), .out(_5_add));  // open: cin, cout
  not not_1 (not_1_out, Y[31]);
  not not_2 (not_2_out, X[31]);
  xnor xnor_1 (xnor_1_out, Y[31], X[31]);
  and and_2 (and_2_out, X[31], not_1_out);
  Subtractor #(.width(32)) subtractor_2 (.a(X), .b(Y), .out(_7_sub));  // open: bin, bout
  and and_3 (and_3_out, Y[31], not_2_out);
  Comparator #(.width(4)) comparator_4 (.a(4'b0101), .b(Switch), .eq(comparator_4_eq));  // open: gt, lt
  Comparator #(.width(4)) comparator_5 (.a(4'b0111), .b(Switch), .eq(comparator_5_eq));  // open: gt, lt
  Multiplexer #(.select(4), .width(32)) multiplexer_1 (
    .in0(_0_sll), .in1(_1_srl), .in2(_2_sra), .in5(_5_add), .in6(_6_addu), .in7(_7_sub), .in8(_8_subu),
    .in9(_9_and), .in10(_10_or), .in11(_11_slt), .in12(_12_sltu), .in15({32{1'b0}}), .out(Result),
    .sel(Switch));  // open: in3, in4, in13, in14, en
  xor xor_1 (xor_1_out, X[31], _5_add[31]);
  not not_3 (not_3_out, _7_sub[31]);
  or or_2 (or_2_out, comparator_4_eq, comparator_5_eq);
  and and_4 (and_4_out, xnor_1_out, xor_1_out);
  and and_5 (and_5_out, and_2_out, not_3_out);
  and and_6 (and_6_out, _7_sub[31], and_3_out);
  Transistor transistor_1 (.in(1'b0), .out(Signed_Overflow), .gate(or_2_out));
  Comparator #(.width(4)) comparator_6 (.a(4'b0101), .b(Switch), .eq(comparator_6_eq));  // open: gt, lt
  not not_4 (not_4_out, comparator_6_eq);
  Transistor transistor_2 (.in(and_4_out), .out(Signed_Overflow), .gate(not_4_out));
  or or_3 (or_3_out, and_5_out, and_6_out);
  not not_5 (not_5_out, comparator_7_eq);
  Comparator #(.width(4)) comparator_7 (.a(4'b0111), .b(Switch), .eq(comparator_7_eq));  // open: gt, lt
  Transistor transistor_3 (.in(or_3_out), .out(Signed_Overflow), .gate(not_5_out));

  // Other names for the same wires on the sheet: overflow = Signed_Overflow; S[3:0] = Switch

  // Notes on the sheet:
  //   INPUTS to your circuit
  //   DON'T CHANGE THE LOCATIONS OF THE INPUTS AND OUTPUTS!
  //   OUTPUTS from your circuit
endmodule
