// Logisim project cpu.circ as structural Verilog: 2 circuits, main circuit main
module main (
  input  [31:0] INSTRUCTION,
  input  CLOCK,
  output [31:0] FETCH_ADDRESS,
  output [31:0] s0_Value,
  output [31:0] s1_Value,
  output [31:0] s2_Value,
  output [31:0] ra_Value,
  output [31:0] sp_Value
);

  wire ALUsrc, and_1_out, and_2_out, and_3_out, branchEqual, branchNotEqual, branchOverflow, ExtOp,
       goToBranch, jump, jumpAndLink, jumpRegister, LUI, main_2_equal, main_2_signed_overflow, MemtoReg,
       MemWr, nop, not_1_out, or_2_out, RegDst, RegWr, shift;
  wire [3:0] ALUctr;
  wire [4:0] multiplexer_1_out, multiplexer_2_out;
  wire [5:0] funct, opcode;
  wire [15:6] immediate;
  wire [25:0] j_address;
  wire [25:16] pipelined;
  wire [31:0] adder_1_out, adder_2_out, afterShift, and_4_out, bit_extender_1_out, bit_extender_2_out,
       bit_extender_4_out, bit_extender_5_out, branchAddress, dataInMem, extended, jumpAddress, jumpReg,
       main_2_result, main_3_p5, multiplexer_4_out, multiplexer_5_out, multiplexer_6_out, multiplexer_10_out,
       PC_4, shifter_1_out, shifter_2_out, shifter_3_out, try, writeData, writeDataNorm;

  Multiplexer #(.width(5)) multiplexer_1 (
    .in0(pipelined[20:16]), .in1(immediate[15:11]), .out(multiplexer_1_out), .sel(RegDst));  // open: en
  Multiplexer #(.width(5)) multiplexer_2 (
    .in0(multiplexer_1_out), .in1({5{1'b1}}), .out(multiplexer_2_out), .sel(jumpAndLink));  // open: en
  // Probe on {opcode, pipelined, immediate, funct}
  assign bit_extender_1_out = {{16{1'b0}}, {immediate, funct}};  // Bit_Extender bit_extender_1
  assign bit_extender_2_out = {{16{immediate[15]}}, {immediate, funct}};  // Bit_Extender bit_extender_2
  Bit_Extender #(.in_width(32), .out_width(26)) bit_extender_3 (
    .in({opcode, pipelined, immediate, funct}), .out(j_address));
  regfile_main main_1 (
    .Read_Register_1(pipelined[25:21]), .Read_Register_2(pipelined[20:16]),
    .Write_Register(multiplexer_2_out), .Write_Data(writeData), .Write_Enable(RegWr), .Clock(CLOCK),
    .Read_Data_1(jumpReg), .Read_Data_2(dataInMem), .s0_Value(s0_Value), .s1_Value(s1_Value),
    .s2_Value(s2_Value), .ra_Value(ra_Value), .sp_Value(sp_Value));
  // Probe on extended
  Multiplexer #(.width(32)) multiplexer_3 (
    .in0(bit_extender_1_out), .in1(bit_extender_2_out), .out(extended), .sel(ExtOp));  // open: en
  Multiplexer #(.width(32)) multiplexer_4 (
    .in0(dataInMem), .in1(extended), .out(multiplexer_4_out), .sel(ALUsrc));  // open: en
  and and_1 (and_1_out, branchOverflow, main_2_signed_overflow);
  LED led_1 (.in(main_2_signed_overflow));
  alu_main main_2 (
    .Switch(ALUctr), .X(afterShift), .Equal(main_2_equal), .Result(main_2_result),
    .Signed_Overflow(main_2_signed_overflow), .Y(multiplexer_4_out));
  or or_1 (goToBranch, and_1_out, and_2_out, and_3_out);
  and and_2 (and_2_out, main_2_equal, branchEqual);
  LED led_2 ();  // open: in
  and and_3 (and_3_out, not_1_out, branchNotEqual);
  not not_1 (not_1_out, main_2_equal);
  Shifter #(.width(32)) shifter_1 (.in(extended), .\dist (5'b00010), .out(shifter_1_out));
  assign bit_extender_4_out = {{6{1'b0}}, j_address};  // Bit_Extender bit_extender_4
  // mem_main main_3: pin names not known; wires that end beside it: main_2_result, dataInMem, MemWr, CLOCK, main_3_p5, MemtoReg
  Adder #(.width(32)) adder_1 (.a(try), .b(shifter_1_out), .out(adder_1_out));  // open: cin, cout
  assign and_4_out = FETCH_ADDRESS & 32'hf0000000;  // AND_Gate and_4, 32 bits wide
  Shifter #(.width(32)) shifter_2 (.in(bit_extender_4_out), .\dist (5'b00010), .out(shifter_2_out));
  Register #(.width(32)) PC (.D(multiplexer_5_out), .Q(FETCH_ADDRESS), .clk(CLOCK));  // open: en, clr
  Multiplexer #(.width(32)) multiplexer_5 (
    .in0(branchAddress), .in1(jumpAddress), .out(multiplexer_5_out), .sel(jump));  // open: en
  Shifter #(.width(32)) shifter_3 (.in(extended), .\dist (5'b10000), .out(shifter_3_out));
  Multiplexer #(.width(32)) multiplexer_6 (
    .in0(INSTRUCTION), .in1({32{1'b0}}), .out(multiplexer_6_out), .sel(nop));  // open: en
  // Probe on nop
  Multiplexer #(.width(32)) multiplexer_7 (
    .in0(main_2_result), .in1(main_3_p5), .out(writeDataNorm), .sel(MemtoReg));  // open: en
  Multiplexer #(.width(32)) multiplexer_8 (
    .in0(PC_4), .in1(adder_1_out), .out(branchAddress), .sel(goToBranch));  // open: en
  Adder #(.width(32)) adder_2 (.a(and_4_out), .b(shifter_2_out), .out(adder_2_out));  // open: cin, cout
  Multiplexer #(.width(32)) multiplexer_9 (
    .in0(adder_2_out), .in1(jumpReg), .out(jumpAddress), .sel(jumpRegister));  // open: en
  Multiplexer #(.width(32)) multiplexer_10 (
    .in0(writeDataNorm), .in1(shifter_3_out), .out(multiplexer_10_out), .sel(LUI));  // open: en
  Register #(.width(32)) pipelineReg (
    .D(multiplexer_6_out), .Q({opcode, pipelined, immediate, funct}), .clk(CLOCK));  // open: en, clr
  Adder #(.width(32)) adder_3 (.a(32'h4), .b(FETCH_ADDRESS), .out(PC_4));  // open: cin, cout
  Multiplexer #(.width(32)) multiplexer_11 (
    .in0(multiplexer_10_out), .in1(FETCH_ADDRESS), .out(writeData), .sel(jumpAndLink));  // open: en
  assign bit_extender_5_out = {{27{1'b0}}, immediate[10:6]};  // Bit_Extender bit_extender_5
  or or_2 (or_2_out, jump, jumpRegister);
  Multiplexer #(.width(32)) multiplexer_12 (
    .in0(jumpReg), .in1(bit_extender_5_out), .out(afterShift), .sel(shift));  // open: en
  control control_1 (
    .shamt(immediate[10:6]), .rd(immediate[15:11]), .rt(pipelined[20:16]), .rs(pipelined[25:21]),
    .immediate({immediate, funct}), .j_address(j_address), .funct(funct), .opcode(opcode), .ExtOp(ExtOp),
    .ALUsrc(ALUsrc), .ALUctr(ALUctr), .MemWr(MemWr), .MemtoReg(MemtoReg), .RegDst(RegDst), .RegWr(RegWr),
    .jump(jump), .branchOverflow(branchOverflow), .LUI(LUI), .branchEqual(branchEqual),
    .branchNotEqual(branchNotEqual), .jumpRegister(jumpRegister), .jumpAndLink(jumpAndLink), .shift(shift));
  or or_3 (nop, or_2_out, goToBranch);

  // Other names for the same wires on the sheet: clk = CLOCK; immediate[5:0] = funct;
  //   pipelined (some bits) = {opcode, immediate, funct}; shamt[4:0] = immediate[10:6]; rd[4:0] = immediate[15:11];
  //   rt[4:0] = pipelined[20:16]; rs[4:0] = pipelined[25:21]; ra[31:0] = ra_Value; s0[31:0] = s0_Value;
  //   s1[31:0] = s1_Value; s2[31:0] = s2_Value; sp[31:0] = sp_Value; fetch_addr[31:0] = FETCH_ADDRESS;
  //   thisPC[31:0] = FETCH_ADDRESS

  // Notes on the sheet:
  //   Output
  //   decompose of instruction
  //   These are outputs/inputs from run.circ
  //   imm extend
  //   Inputs
  //   rs
  //   rt
  //   R type
  //   I-type
  //   J-type
  //   lui is special becuase it needs imm to transform
  //   ** not sure if -16 shifting is okay!
  //   These are DEBUG/TEST outputs from your circuit.
  //   PC+4, fetch instruction, jump and branch
  //   decide shamt
  //   control and decode
endmodule

module control (
  input  [5:0] funct,
  input  [4:0] shamt,
  input  [4:0] rd,
  input  [4:0] rt,
  input  [4:0] rs,
  input  [5:0] opcode,
  input  [15:0] immediate,
  input  [25:0] j_address,
  output ExtOp,
  output ALUsrc,
  output [3:0] ALUctr,
  output MemWr,
  output MemtoReg,
  output RegDst,
  output RegWr,
  output jump,
  output branchOverflow,
  output LUI,
  output branchEqual,
  output branchNotEqual,
  output jumpRegister,
  output jumpAndLink,
  output shift
);

  wire ADD, ADDI, ADDIU, ADDU, AND, ANDI, comparator_1_eq, comparator_3_eq, comparator_4_eq, comparator_5_eq,
       comparator_6_eq, comparator_7_eq, comparator_8_eq, comparator_9_eq, comparator_10_eq,
       comparator_11_eq, comparator_12_eq, comparator_13_eq, comparator_14_eq, comparator_15_eq,
       comparator_16_eq, comparator_17_eq, comparator_18_eq, comparator_19_eq, comparator_20_eq,
       comparator_21_eq, comparator_22_eq, comparator_23_eq, comparator_24_eq, comparator_25_eq,
       comparator_26_eq, J, JAL, JALR, JR, not_1_out, OR, or_1_out, or_3_out, or_4_out, or_5_out, or_6_out,
       ORI, SLL, SLT, SLTI, SLTIU, SLTU, SRA, SRL, SUB, SUBU;

  Comparator #(.width(6), .mode("unsigned")) comparator_1 (
    .a(6'b100000), .b(funct), .eq(comparator_1_eq));  // open: gt, lt
  Comparator #(.width(6), .mode("unsigned")) comparator_2 (.a(opcode), .b({6{1'b0}}), .eq(RegDst));  // open: gt, lt
  Comparator #(.width(6), .mode("unsigned")) comparator_3 (
    .a(6'b100001), .b(funct), .eq(comparator_3_eq));  // open: gt, lt
  Comparator #(.width(6), .mode("unsigned")) comparator_4 (
    .a(opcode), .b({6{1'b0}}), .eq(comparator_4_eq));  // open: gt, lt
  Comparator #(.width(6), .mode("unsigned")) comparator_5 (
    .a(6'b100100), .b(funct), .eq(comparator_5_eq));  // open: gt, lt
  Comparator #(.width(6), .mode("unsigned")) comparator_6 (
    .a(opcode), .b({6{1'b0}}), .eq(comparator_6_eq));  // open: gt, lt
  Comparator #(.width(6), .mode("unsigned")) comparator_7 (
    .a(6'b001000), .b(funct), .eq(comparator_7_eq));  // open: gt, lt
  Comparator #(.width(6), .mode("unsigned")) comparator_8 (
    .a(opcode), .b({6{1'b0}}), .eq(comparator_8_eq));  // open: gt, lt
  Comparator #(.width(6), .mode("unsigned")) comparator_9 (
    .a(6'b001001), .b(funct), .eq(comparator_9_eq));  // open: gt, lt
  Comparator #(.width(6), .mode("unsigned")) comparator_10 (
    .a(opcode), .b({6{1'b0}}), .eq(comparator_10_eq));  // open: gt, lt
  Comparator #(.width(6), .mode("unsigned")) comparator_11 (
    .a(6'b100101), .b(funct), .eq(comparator_11_eq));  // open: gt, lt
  Comparator #(.width(6), .mode("unsigned")) comparator_12 (
    .a(opcode), .b({6{1'b0}}), .eq(comparator_12_eq));  // open: gt, lt
  Comparator #(.width(6), .mode("unsigned")) comparator_13 (
    .a(6'b101010), .b(funct), .eq(comparator_13_eq));  // open: gt, lt
  Comparator #(.width(6), .mode("unsigned")) comparator_14 (
    .a(opcode), .b({6{1'b0}}), .eq(comparator_14_eq));  // open: gt, lt
  Comparator #(.width(6), .mode("unsigned")) comparator_15 (
    .a(6'b101011), .b(funct), .eq(comparator_15_eq));  // open: gt, lt
  Comparator #(.width(6), .mode("unsigned")) comparator_16 (
    .a(opcode), .b({6{1'b0}}), .eq(comparator_16_eq));  // open: gt, lt
  Comparator #(.width(6), .mode("unsigned")) comparator_17 (
    .a({6{1'b0}}), .b(funct), .eq(comparator_17_eq));  // open: gt, lt
  Comparator #(.width(6), .mode("unsigned")) comparator_18 (
    .a(opcode), .b({6{1'b0}}), .eq(comparator_18_eq));  // open: gt, lt
  Comparator #(.width(6), .mode("unsigned")) comparator_19 (
    .a(6'b000011), .b(funct), .eq(comparator_19_eq));  // open: gt, lt
  Comparator #(.width(6), .mode("unsigned")) comparator_20 (
    .a(opcode), .b({6{1'b0}}), .eq(comparator_20_eq));  // open: gt, lt
  Comparator #(.width(6), .mode("unsigned")) comparator_21 (
    .a(6'b000010), .b(funct), .eq(comparator_21_eq));  // open: gt, lt
  Comparator #(.width(6), .mode("unsigned")) comparator_22 (
    .a(opcode), .b({6{1'b0}}), .eq(comparator_22_eq));  // open: gt, lt
  Comparator #(.width(6), .mode("unsigned")) comparator_23 (
    .a(6'b100010), .b(funct), .eq(comparator_23_eq));  // open: gt, lt
  Comparator #(.width(6), .mode("unsigned")) comparator_24 (
    .a(opcode), .b({6{1'b0}}), .eq(comparator_24_eq));  // open: gt, lt
  Comparator #(.width(6), .mode("unsigned")) comparator_25 (
    .a(6'b100011), .b(funct), .eq(comparator_25_eq));  // open: gt, lt
  Comparator #(.width(6), .mode("unsigned")) comparator_26 (
    .a(opcode), .b({6{1'b0}}), .eq(comparator_26_eq));  // open: gt, lt
  // Probe on ALUctr
  and and_1 (ADD, comparator_1_eq, RegDst);
  and and_2 (ADDU, comparator_3_eq, comparator_4_eq);
  and and_3 (AND, comparator_5_eq, comparator_6_eq);
  and and_4 (JR, comparator_7_eq, comparator_8_eq);
  and and_5 (JALR, comparator_9_eq, comparator_10_eq);
  and and_6 (OR, comparator_11_eq, comparator_12_eq);
  and and_7 (SLT, comparator_13_eq, comparator_14_eq);
  and and_8 (SLTU, comparator_15_eq, comparator_16_eq);
  and and_9 (SLL, comparator_17_eq, comparator_18_eq);
  and and_10 (SRA, comparator_19_eq, comparator_20_eq);
  and and_11 (SRL, comparator_21_eq, comparator_22_eq);
  and and_12 (SUB, comparator_23_eq, comparator_24_eq);
  and and_13 (SUBU, comparator_25_eq, comparator_26_eq);
  assign ALUctr = not_1_out ? 4'b1111 : 4'bz;  // Controlled_Buffer controlled_buffer_1
  not not_1 (not_1_out, or_1_out);
  or or_1 (or_1_out, or_3_out, or_4_out, or_5_out, or_6_out);
  or or_2 (shift, SLL, SRA, SRL);
  or or_3 (or_3_out, ADD, ADDU, AND, OR, SLT);
  or or_4 (or_4_out, SLTU, SLL, SRA, SRL, SUB);
  or or_5 (or_5_out, SUBU, ADDI, ADDIU, ANDI, branchOverflow);
  or or_6 (or_6_out, MemtoReg, ORI, SLTI, SLTIU, MemWr);
  assign ALUctr = ADD ? 4'b0101 : 4'bz;  // Controlled_Buffer controlled_buffer_2
  assign ALUctr = ADDU ? 4'b0110 : 4'bz;  // Controlled_Buffer controlled_buffer_3
  assign ALUctr = AND ? 4'b1001 : 4'bz;  // Controlled_Buffer controlled_buffer_4
  assign ALUctr = OR ? 4'b1010 : 4'bz;  // Controlled_Buffer controlled_buffer_5
  assign ALUctr = SLT ? 4'b1011 : 4'bz;  // Controlled_Buffer controlled_buffer_6
  assign ALUctr = SLTU ? 4'b1100 : 4'bz;  // Controlled_Buffer controlled_buffer_7
  assign ALUctr = SLL ? 4'b0000 : 4'bz;  // Controlled_Buffer controlled_buffer_8
  assign ALUctr = SRA ? 4'b0010 : 4'bz;  // Controlled_Buffer controlled_buffer_9
  assign ALUctr = SRL ? 4'b0001 : 4'bz;  // Controlled_Buffer controlled_buffer_10
  assign ALUctr = SUB ? 4'b0111 : 4'bz;  // Controlled_Buffer controlled_buffer_11
  assign ALUctr = SUBU ? 4'b1000 : 4'bz;  // Controlled_Buffer controlled_buffer_12
  LED led_1 ();  // open: in
  or or_7 (ALUsrc, ADDI, ADDIU, ANDI, MemtoReg, LUI, ORI, SLTI, SLTIU, MemWr);
  or or_8 (jumpAndLink, JAL, JALR);
  or or_9 (jumpRegister, JALR, JR);
  Comparator #(.width(6), .mode("unsigned")) comparator_27 (.a(opcode), .b(6'b001000), .eq(ADDI));  // open: gt, lt
  Comparator #(.width(6), .mode("unsigned")) comparator_28 (.a(opcode), .b(6'b001001), .eq(ADDIU));  // open: gt, lt
  Comparator #(.width(6), .mode("unsigned")) comparator_29 (.a(opcode), .b(6'b001100), .eq(ANDI));  // open: gt, lt
  Comparator #(.width(6), .mode("unsigned")) comparator_30 (
    .a(opcode), .b(6'b000100), .eq(branchEqual));  // open: gt, lt
  Comparator #(.width(6), .mode("unsigned")) comparator_31 (
    .a(opcode), .b(6'b000101), .eq(branchNotEqual));  // open: gt, lt
  Comparator #(.width(6), .mode("unsigned")) comparator_32 (
    .a(opcode), .b(6'b000110), .eq(branchOverflow));  // open: gt, lt
  Comparator #(.width(6), .mode("unsigned")) comparator_33 (.a(opcode), .b(6'b000010), .eq(J));  // open: gt, lt
  Comparator #(.width(6), .mode("unsigned")) comparator_34 (.a(opcode), .b(6'b000011), .eq(JAL));  // open: gt, lt
  Comparator #(.width(6), .mode("unsigned")) comparator_35 (.a(opcode), .b(6'b001111), .eq(LUI));  // open: gt, lt
  Comparator #(.width(6), .mode("unsigned")) comparator_36 (.a(opcode), .b(6'b100011), .eq(MemtoReg));  // open: gt, lt
  Comparator #(.width(6), .mode("unsigned")) comparator_37 (.a(opcode), .b(6'b001101), .eq(ORI));  // open: gt, lt
  Comparator #(.width(6), .mode("unsigned")) comparator_38 (.a(opcode), .b(6'b001010), .eq(SLTI));  // open: gt, lt
  Comparator #(.width(6), .mode("unsigned")) comparator_39 (.a(opcode), .b(6'b001011), .eq(SLTIU));  // open: gt, lt
  Comparator #(.width(6), .mode("unsigned")) comparator_40 (.a(opcode), .b(6'b101011), .eq(MemWr));  // open: gt, lt
  or or_10 (RegWr, RegDst, ADDI, ADDIU, ANDI, JAL, LUI, MemtoReg, ORI, SLTI, SLTIU);
  or or_11 (ExtOp, ADDIU, ADDI, MemtoReg, SLTI, MemWr, branchEqual, branchNotEqual, branchOverflow, SLTIU);
  or or_12 (jump, JALR, J, JAL, JR);
  assign ALUctr = ADDI ? 4'b0101 : 4'bz;  // Controlled_Buffer controlled_buffer_13
  assign ALUctr = ADDIU ? 4'b0110 : 4'bz;  // Controlled_Buffer controlled_buffer_14
  assign ALUctr = ANDI ? 4'b1001 : 4'bz;  // Controlled_Buffer controlled_buffer_15
  assign ALUctr = branchOverflow ? 4'b0101 : 4'bz;  // Controlled_Buffer controlled_buffer_16
  assign ALUctr = MemtoReg ? 4'b0110 : 4'bz;  // Controlled_Buffer controlled_buffer_17
  assign ALUctr = ORI ? 4'b1010 : 4'bz;  // Controlled_Buffer controlled_buffer_18
  assign ALUctr = SLTI ? 4'b1011 : 4'bz;  // Controlled_Buffer controlled_buffer_19
  assign ALUctr = SLTIU ? 4'b1011 : 4'bz;  // Controlled_Buffer controlled_buffer_20
  assign ALUctr = MemWr ? 4'b0110 : 4'bz;  // Controlled_Buffer controlled_buffer_21

  // Other names for the same wires on the sheet: BEQ = branchEqual; BNE = branchNotEqual; BOV = branchOverflow;
  //   LW = MemtoReg; RTYPE = RegDst; SW = MemWr

  // Notes on the sheet:
  //   output for reference
  //   input for analyze
  //   R type(11 + 2)
  //   make ALU control == f when not working
  //   to judge if we need shamt
  //   htese need  to write sth in reg
  //   other type(14)
  //   these require src to be imm so src == 1
  //   this means branch control is 1, but really branch or not
  //   alos depends on equal or not equal output from alu
  //   from memory to register
  //   only rtype has rd
  //   only sw (sb) needs to write in memory data
  //   in these cases the pc will change
  //   decide who need a sign extension
  //   **make sure that unsign should extend zero, and signed extend sign
  //   these don't need regwr, put here as reference
endmodule
