// Logisim project regfile.circ as structural Verilog: 1 circuit, main circuit main
module main (
  input  [4:0] Read_Register_1,
  input  [4:0] Read_Register_2,
  input  [4:0] Write_Register,
  input  [31:0] Write_Data,
  input  Write_Enable,
  input  Clock,
  output [31:0] s0_Value,
  output [31:0] s1_Value,
  output [31:0] s2_Value,
  output [31:0] ra_Value,
  output [31:0] sp_Value,
  output [31:0] Read_Data_1,
  output [31:0] Read_Data_2
);

  wire and_1_out, and_2_out, and_3_out, and_4_out, and_5_out, and_6_out, and_7_out, and_8_out, and_9_out,
       and_10_out, and_11_out, and_12_out, and_13_out, and_14_out, and_15_out, and_16_out, and_17_out,
       and_18_out, and_19_out, and_20_out, and_21_out, and_22_out, and_23_out, and_24_out, and_25_out,
       and_26_out, and_27_out, and_28_out, and_29_out, and_30_out, and_31_out, comparator_1_eq,
       comparator_2_eq, comparator_3_eq, comparator_4_eq, comparator_5_eq, comparator_6_eq, comparator_7_eq,
       comparator_8_eq, comparator_9_eq, comparator_10_eq, comparator_11_eq, comparator_12_eq,
       comparator_13_eq, comparator_14_eq, comparator_15_eq, comparator_16_eq, comparator_17_eq,
       comparator_18_eq, comparator_19_eq, comparator_20_eq, comparator_21_eq, comparator_22_eq,
       comparator_23_eq, comparator_24_eq, comparator_25_eq, comparator_26_eq, comparator_27_eq,
       comparator_28_eq, comparator_29_eq, comparator_30_eq, comparator_31_eq, comparator_32_eq,
       comparator_33_eq, comparator_34_eq, comparator_35_eq, comparator_36_eq, comparator_37_eq,
       comparator_38_eq, comparator_39_eq, comparator_40_eq, comparator_41_eq, comparator_42_eq,
       comparator_43_eq, comparator_44_eq, comparator_45_eq, comparator_46_eq, comparator_47_eq,
       comparator_48_eq, comparator_49_eq, comparator_50_eq, comparator_51_eq, comparator_52_eq,
       comparator_53_eq, comparator_54_eq, comparator_55_eq, comparator_56_eq, comparator_57_eq,
       comparator_58_eq, comparator_59_eq, comparator_60_eq, comparator_61_eq, comparator_62_eq,
       comparator_63_eq, comparator_64_eq, comparator_65_eq, comparator_66_eq, comparator_67_eq,
       comparator_68_eq, comparator_69_eq, comparator_70_eq, comparator_71_eq, comparator_72_eq,
       comparator_73_eq, comparator_74_eq, comparator_75_eq, comparator_76_eq, comparator_77_eq,
       comparator_78_eq, comparator_79_eq, comparator_80_eq, comparator_81_eq, comparator_82_eq,
       comparator_83_eq, comparator_84_eq, comparator_85_eq, comparator_86_eq, comparator_87_eq,
       comparator_88_eq, comparator_89_eq, comparator_90_eq, comparator_91_eq, comparator_92_eq,
       comparator_93_eq, comparator_94_eq, comparator_95_eq, comparator_96_eq, comparator_97_eq,
       comparator_98_eq, comparator_99_eq, comparator_100_eq, comparator_101_eq, comparator_102_eq,
       comparator_103_eq, comparator_104_eq, comparator_105_eq, comparator_106_eq, comparator_107_eq,
       comparator_108_eq, comparator_109_eq, comparator_110_eq, comparator_111_eq, comparator_112_eq,
       comparator_113_eq, comparator_114_eq, comparator_115_eq, comparator_116_eq, comparator_117_eq,
       comparator_118_eq, comparator_119_eq, comparator_120_eq, comparator_121_eq, comparator_122_eq,
       comparator_123_eq, comparator_124_eq, comparator_125_eq, comparator_126_eq, not_1_out, not_2_out,
       not_3_out, not_4_out, not_5_out, not_6_out, not_7_out, not_8_out, not_9_out, not_10_out, not_11_out,
       not_12_out, not_13_out, not_14_out, not_15_out, not_16_out, not_17_out, not_18_out, not_19_out,
       not_20_out, not_21_out, not_22_out, not_23_out, not_24_out, not_25_out, not_26_out, not_27_out,
       not_28_out, not_29_out, not_30_out, not_31_out, not_32_out, not_33_out, not_34_out, not_35_out,
       not_36_out, not_37_out, not_38_out, not_39_out, not_40_out, not_41_out, not_42_out, not_43_out,
       not_44_out, not_45_out, not_46_out, not_47_out, not_48_out, not_49_out, not_50_out, not_51_out,
       not_52_out, not_53_out, not_54_out, not_55_out, not_56_out, not_57_out, not_58_out, not_59_out,
       not_60_out, not_61_out, not_62_out, not_63_out, not_64_out;
  wire [31:0] register_1_q, register_2_q, register_3_q, register_4_q, register_5_q, register_6_q,
       register_7_q, register_8_q, register_10_q, register_11_q, register_12_q, register_13_q, register_14_q,
       register_15_q, register_16_q, register_19_q, register_20_q, register_21_q, register_22_q,
       register_23_q, register_24_q, register_25_q, register_26_q, register_27_q, register_28_q,
       register_30_q, register_32_q;

  // Probe on Read_Register_1
  Comparator #(.width(5)) comparator_1 (.a(5'b00001), .b(Write_Register), .eq(comparator_1_eq));  // open: gt, lt
  Comparator #(.width(1)) comparator_2 (.a(Write_Enable), .b(1'b1), .eq(comparator_2_eq));  // open: gt, lt
  Comparator #(.width(5)) comparator_3 (.a(5'b00010), .b(Write_Register), .eq(comparator_3_eq));  // open: gt, lt
  Comparator #(.width(1)) comparator_4 (.a(Write_Enable), .b(1'b1), .eq(comparator_4_eq));  // open: gt, lt
  Comparator #(.width(5)) comparator_5 (.a(5'b00011), .b(Write_Register), .eq(comparator_5_eq));  // open: gt, lt
  Comparator #(.width(1)) comparator_6 (.a(Write_Enable), .b(1'b1), .eq(comparator_6_eq));  // open: gt, lt
  Comparator #(.width(5)) comparator_7 (.a(5'b00100), .b(Write_Register), .eq(comparator_7_eq));  // open: gt, lt
  Comparator #(.width(1)) comparator_8 (.a(Write_Enable), .b(1'b1), .eq(comparator_8_eq));  // open: gt, lt
  Comparator #(.width(5)) comparator_9 (.a(5'b00101), .b(Write_Register), .eq(comparator_9_eq));  // open: gt, lt
  Comparator #(.width(1)) comparator_10 (.a(Write_Enable), .b(1'b1), .eq(comparator_10_eq));  // open: gt, lt
  Comparator #(.width(5)) comparator_11 (.a(5'b00110), .b(Write_Register), .eq(comparator_11_eq));  // open: gt, lt
  Comparator #(.width(1)) comparator_12 (.a(Write_Enable), .b(1'b1), .eq(comparator_12_eq));  // open: gt, lt
  Comparator #(.width(5)) comparator_13 (.a(5'b00111), .b(Write_Register), .eq(comparator_13_eq));  // open: gt, lt
  Comparator #(.width(1)) comparator_14 (.a(Write_Enable), .b(1'b1), .eq(comparator_14_eq));  // open: gt, lt
  and and_1 (and_1_out, comparator_1_eq, comparator_2_eq);
  and and_2 (and_2_out, comparator_3_eq, comparator_4_eq);
  and and_3 (and_3_out, comparator_5_eq, comparator_6_eq);
  and and_4 (and_4_out, comparator_7_eq, comparator_8_eq);
  and and_5 (and_5_out, comparator_9_eq, comparator_10_eq);
  and and_6 (and_6_out, comparator_11_eq, comparator_12_eq);
  and and_7 (and_7_out, comparator_13_eq, comparator_14_eq);
  Comparator #(.width(5)) comparator_15 (.a(5'b01000), .b(Write_Register), .eq(comparator_15_eq));  // open: gt, lt
  and and_8 (and_8_out, comparator_15_eq, comparator_16_eq);
  Comparator #(.width(1)) comparator_16 (.a(Write_Enable), .b(1'b1), .eq(comparator_16_eq));  // open: gt, lt
  Comparator #(.width(5)) comparator_17 (.a(5'b01001), .b(Write_Register), .eq(comparator_17_eq));  // open: gt, lt
  Comparator #(.width(1)) comparator_18 (.a(Write_Enable), .b(1'b1), .eq(comparator_18_eq));  // open: gt, lt
  Comparator #(.width(5)) comparator_19 (.a(5'b01010), .b(Write_Register), .eq(comparator_19_eq));  // open: gt, lt
  Comparator #(.width(1)) comparator_20 (.a(Write_Enable), .b(1'b1), .eq(comparator_20_eq));  // open: gt, lt
  Comparator #(.width(5)) comparator_21 (.a(5'b01011), .b(Write_Register), .eq(comparator_21_eq));  // open: gt, lt
  Comparator #(.width(1)) comparator_22 (.a(Write_Enable), .b(1'b1), .eq(comparator_22_eq));  // open: gt, lt
  Comparator #(.width(5)) comparator_23 (.a(5'b01100), .b(Write_Register), .eq(comparator_23_eq));  // open: gt, lt
  Comparator #(.width(1)) comparator_24 (.a(Write_Enable), .b(1'b1), .eq(comparator_24_eq));  // open: gt, lt
  Comparator #(.width(5)) comparator_25 (.a(5'b01101), .b(Write_Register), .eq(comparator_25_eq));  // open: gt, lt
  Comparator #(.width(1)) comparator_26 (.a(Write_Enable), .b(1'b1), .eq(comparator_26_eq));  // open: gt, lt
  Comparator #(.width(5)) comparator_27 (.a(5'b01110), .b(Write_Register), .eq(comparator_27_eq));  // open: gt, lt
  Comparator #(.width(1)) comparator_28 (.a(Write_Enable), .b(1'b1), .eq(comparator_28_eq));  // open: gt, lt
  Comparator #(.width(5)) comparator_29 (.a(5'b01111), .b(Write_Register), .eq(comparator_29_eq));  // open: gt, lt
  Comparator #(.width(1)) comparator_30 (.a(Write_Enable), .b(1'b1), .eq(comparator_30_eq));  // open: gt, lt
  Comparator #(.width(5)) comparator_31 (.a(5'b10001), .b(Write_Register), .eq(comparator_31_eq));  // open: gt, lt
  Comparator #(.width(1)) comparator_32 (.a(Write_Enable), .b(1'b1), .eq(comparator_32_eq));  // open: gt, lt
  Comparator #(.width(5)) comparator_33 (.a(5'b10010), .b(Write_Register), .eq(comparator_33_eq));  // open: gt, lt
  Comparator #(.width(1)) comparator_34 (.a(Write_Enable), .b(1'b1), .eq(comparator_34_eq));  // open: gt, lt
  Comparator #(.width(5)) comparator_35 (.a(5'b10011), .b(Write_Register), .eq(comparator_35_eq));  // open: gt, lt
  Comparator #(.width(1)) comparator_36 (.a(Write_Enable), .b(1'b1), .eq(comparator_36_eq));  // open: gt, lt
  Comparator #(.width(5)) comparator_37 (.a(5'b10100), .b(Write_Register), .eq(comparator_37_eq));  // open: gt, lt
  Comparator #(.width(1)) comparator_38 (.a(Write_Enable), .b(1'b1), .eq(comparator_38_eq));  // open: gt, lt
  Comparator #(.width(5)) comparator_39 (.a(5'b10101), .b(Write_Register), .eq(comparator_39_eq));  // open: gt, lt
  Comparator #(.width(1)) comparator_40 (.a(Write_Enable), .b(1'b1), .eq(comparator_40_eq));  // open: gt, lt
  Comparator #(.width(5)) comparator_41 (.a(5'b10110), .b(Write_Register), .eq(comparator_41_eq));  // open: gt, lt
  Comparator #(.width(1)) comparator_42 (.a(Write_Enable), .b(1'b1), .eq(comparator_42_eq));  // open: gt, lt
  Comparator #(.width(5)) comparator_43 (.a(5'b10111), .b(Write_Register), .eq(comparator_43_eq));  // open: gt, lt
  Comparator #(.width(1)) comparator_44 (.a(Write_Enable), .b(1'b1), .eq(comparator_44_eq));  // open: gt, lt
  Comparator #(.width(5)) comparator_45 (.a(5'b11000), .b(Write_Register), .eq(comparator_45_eq));  // open: gt, lt
  Comparator #(.width(1)) comparator_46 (.a(Write_Enable), .b(1'b1), .eq(comparator_46_eq));  // open: gt, lt
  Register #(.width(32)) register_1 (.D(Write_Data), .en(and_1_out), .Q(register_1_q), .clk(Clock));  // open: clr
  Register #(.width(32)) register_2 (.D(Write_Data), .en(and_2_out), .Q(register_2_q), .clk(Clock));  // open: clr
  Register #(.width(32)) register_3 (.D(Write_Data), .en(and_3_out), .Q(register_3_q), .clk(Clock));  // open: clr
  Register #(.width(32)) register_4 (.D(Write_Data), .en(and_4_out), .Q(register_4_q), .clk(Clock));  // open: clr
  Register #(.width(32)) register_5 (.D(Write_Data), .en(and_5_out), .Q(register_5_q), .clk(Clock));  // open: clr
  Register #(.width(32)) register_6 (.D(Write_Data), .en(and_6_out), .Q(register_6_q), .clk(Clock));  // open: clr
  Register #(.width(32)) register_7 (.D(Write_Data), .en(and_7_out), .Q(register_7_q), .clk(Clock));  // open: clr
  Register #(.width(32)) register_8 (.D(Write_Data), .en(and_8_out), .Q(register_8_q), .clk(Clock));  // open: clr
  and and_9 (and_9_out, comparator_17_eq, comparator_18_eq);
  and and_10 (and_10_out, comparator_19_eq, comparator_20_eq);
  and and_11 (and_11_out, comparator_21_eq, comparator_22_eq);
  and and_12 (and_12_out, comparator_23_eq, comparator_24_eq);
  and and_13 (and_13_out, comparator_25_eq, comparator_26_eq);
  and and_14 (and_14_out, comparator_27_eq, comparator_28_eq);
  and and_15 (and_15_out, comparator_29_eq, comparator_30_eq);
  Comparator #(.width(5)) comparator_47 (.a(5'b10000), .b(Write_Register), .eq(comparator_47_eq));  // open: gt, lt
  and and_16 (and_16_out, comparator_47_eq, comparator_48_eq);
  Comparator #(.width(1)) comparator_48 (.a(Write_Enable), .b(1'b1), .eq(comparator_48_eq));  // open: gt, lt
  Register #(.width(32)) register_9 (.D(Write_Data), .en(and_17_out), .Q(s1_Value), .clk(Clock));  // open: clr
  and and_17 (and_17_out, comparator_31_eq, comparator_32_eq);
  and and_18 (and_18_out, comparator_33_eq, comparator_34_eq);
  and and_19 (and_19_out, comparator_35_eq, comparator_36_eq);
  and and_20 (and_20_out, comparator_37_eq, comparator_38_eq);
  and and_21 (and_21_out, comparator_39_eq, comparator_40_eq);
  and and_22 (and_22_out, comparator_41_eq, comparator_42_eq);
  and and_23 (and_23_out, comparator_43_eq, comparator_44_eq);
  and and_24 (and_24_out, comparator_45_eq, comparator_46_eq);
  Comparator #(.width(5)) comparator_49 (.a(5'b11001), .b(Write_Register), .eq(comparator_49_eq));  // open: gt, lt
  Comparator #(.width(1)) comparator_50 (.a(Write_Enable), .b(1'b1), .eq(comparator_50_eq));  // open: gt, lt
  Comparator #(.width(5)) comparator_51 (.a(5'b11010), .b(Write_Register), .eq(comparator_51_eq));  // open: gt, lt
  Comparator #(.width(1)) comparator_52 (.a(Write_Enable), .b(1'b1), .eq(comparator_52_eq));  // open: gt, lt
  Comparator #(.width(5)) comparator_53 (.a(5'b11011), .b(Write_Register), .eq(comparator_53_eq));  // open: gt, lt
  Comparator #(.width(1)) comparator_54 (.a(Write_Enable), .b(1'b1), .eq(comparator_54_eq));  // open: gt, lt
  Comparator #(.width(5)) comparator_55 (.a(5'b11100), .b(Write_Register), .eq(comparator_55_eq));  // open: gt, lt
  Comparator #(.width(1)) comparator_56 (.a(Write_Enable), .b(1'b1), .eq(comparator_56_eq));  // open: gt, lt
  Comparator #(.width(5)) comparator_57 (.a(5'b11101), .b(Write_Register), .eq(comparator_57_eq));  // open: gt, lt
  Comparator #(.width(1)) comparator_58 (.a(Write_Enable), .b(1'b1), .eq(comparator_58_eq));  // open: gt, lt
  Comparator #(.width(5)) comparator_59 (.a(5'b11110), .b(Write_Register), .eq(comparator_59_eq));  // open: gt, lt
  Comparator #(.width(1)) comparator_60 (.a(Write_Enable), .b(1'b1), .eq(comparator_60_eq));  // open: gt, lt
  Comparator #(.width(5)) comparator_61 (.a({5{1'b1}}), .b(Write_Register), .eq(comparator_61_eq));  // open: gt, lt
  Comparator #(.width(1)) comparator_62 (.a(Write_Enable), .b(1'b1), .eq(comparator_62_eq));  // open: gt, lt
  Comparator #(.width(5), .mode("unsigned")) comparator_63 (
    .a(5'b00001), .b(Read_Register_2), .eq(comparator_63_eq));  // open: gt, lt
  Comparator #(.width(5), .mode("unsigned")) comparator_64 (
    .a(5'b00001), .b(Read_Register_1), .eq(comparator_64_eq));  // open: gt, lt
  Comparator #(.width(5), .mode("unsigned")) comparator_65 (
    .a(5'b00011), .b(Read_Register_2), .eq(comparator_65_eq));  // open: gt, lt
  Comparator #(.width(5), .mode("unsigned")) comparator_66 (
    .a(5'b00011), .b(Read_Register_1), .eq(comparator_66_eq));  // open: gt, lt
  Register #(.width(32)) register_10 (.D(Write_Data), .en(and_9_out), .Q(register_10_q), .clk(Clock));  // open: clr
  Register #(.width(32)) register_11 (.D(Write_Data), .en(and_10_out), .Q(register_11_q), .clk(Clock));  // open: clr
  Register #(.width(32)) register_12 (.D(Write_Data), .en(and_11_out), .Q(register_12_q), .clk(Clock));  // open: clr
  Register #(.width(32)) register_13 (.D(Write_Data), .en(and_12_out), .Q(register_13_q), .clk(Clock));  // open: clr
  Register #(.width(32)) register_14 (.D(Write_Data), .en(and_13_out), .Q(register_14_q), .clk(Clock));  // open: clr
  Register #(.width(32)) register_15 (.D(Write_Data), .en(and_14_out), .Q(register_15_q), .clk(Clock));  // open: clr
  Register #(.width(32)) register_16 (.D(Write_Data), .en(and_15_out), .Q(register_16_q), .clk(Clock));  // open: clr
  Register #(.width(32)) register_17 (.D(Write_Data), .en(and_16_out), .Q(s0_Value), .clk(Clock));  // open: clr
  Register #(.width(32)) register_18 (.D(Write_Data), .en(and_18_out), .Q(s2_Value), .clk(Clock));  // open: clr
  Register #(.width(32)) register_19 (.D(Write_Data), .en(and_19_out), .Q(register_19_q), .clk(Clock));  // open: clr
  Register #(.width(32)) register_20 (.D(Write_Data), .en(and_20_out), .Q(register_20_q), .clk(Clock));  // open: clr
  Register #(.width(32)) register_21 (.D(Write_Data), .en(and_21_out), .Q(register_21_q), .clk(Clock));  // open: clr
  Register #(.width(32)) register_22 (.D(Write_Data), .en(and_22_out), .Q(register_22_q), .clk(Clock));  // open: clr
  Register #(.width(32)) register_23 (.D(Write_Data), .en(and_23_out), .Q(register_23_q), .clk(Clock));  // open: clr
  Register #(.width(32)) register_24 (.D(Write_Data), .en(and_24_out), .Q(register_24_q), .clk(Clock));  // open: clr
  Register #(.width(32)) register_25 (.D(Write_Data), .en(and_25_out), .Q(register_25_q), .clk(Clock));  // open: clr
  and and_25 (and_25_out, comparator_49_eq, comparator_50_eq);
  and and_26 (and_26_out, comparator_51_eq, comparator_52_eq);
  and and_27 (and_27_out, comparator_53_eq, comparator_54_eq);
  and and_28 (and_28_out, comparator_55_eq, comparator_56_eq);
  and and_29 (and_29_out, comparator_57_eq, comparator_58_eq);
  and and_30 (and_30_out, comparator_59_eq, comparator_60_eq);
  and and_31 (and_31_out, comparator_61_eq, comparator_62_eq);
  not not_1 (not_1_out, comparator_63_eq);
  Transistor #(.width(32)) transistor_1 (.in(register_1_q), .out(Read_Data_2), .gate(not_1_out));
  not not_2 (not_2_out, comparator_64_eq);
  not not_3 (not_3_out, comparator_67_eq);
  Comparator #(.width(5), .mode("unsigned")) comparator_67 (
    .a(5'b00010), .b(Read_Register_2), .eq(comparator_67_eq));  // open: gt, lt
  not not_4 (not_4_out, comparator_68_eq);
  Comparator #(.width(5), .mode("unsigned")) comparator_68 (
    .a(5'b00010), .b(Read_Register_1), .eq(comparator_68_eq));  // open: gt, lt
  not not_5 (not_5_out, comparator_65_eq);
  Transistor #(.width(32)) transistor_2 (.in(register_3_q), .out(Read_Data_2), .gate(not_5_out));
  not not_6 (not_6_out, comparator_66_eq);
  Comparator #(.width(5), .mode("unsigned")) comparator_69 (
    .a(5'b00100), .b(Read_Register_2), .eq(comparator_69_eq));  // open: gt, lt
  not not_7 (not_7_out, comparator_69_eq);
  not not_8 (not_8_out, comparator_70_eq);
  Comparator #(.width(5), .mode("unsigned")) comparator_70 (
    .a(5'b00100), .b(Read_Register_1), .eq(comparator_70_eq));  // open: gt, lt
  not not_9 (not_9_out, comparator_71_eq);
  Comparator #(.width(5), .mode("unsigned")) comparator_71 (
    .a(5'b00101), .b(Read_Register_2), .eq(comparator_71_eq));  // open: gt, lt
  Transistor #(.width(32)) transistor_3 (.in(register_5_q), .out(Read_Data_2), .gate(not_9_out));
  not not_10 (not_10_out, comparator_72_eq);
  Comparator #(.width(5), .mode("unsigned")) comparator_72 (
    .a(5'b00101), .b(Read_Register_1), .eq(comparator_72_eq));  // open: gt, lt
  Comparator #(.width(5), .mode("unsigned")) comparator_73 (
    .a(5'b00110), .b(Read_Register_2), .eq(comparator_73_eq));  // open: gt, lt
  not not_11 (not_11_out, comparator_73_eq);
  Comparator #(.width(5), .mode("unsigned")) comparator_74 (
    .a(5'b00110), .b(Read_Register_1), .eq(comparator_74_eq));  // open: gt, lt
  not not_12 (not_12_out, comparator_74_eq);
  Comparator #(.width(5), .mode("unsigned")) comparator_75 (
    .a(5'b00111), .b(Read_Register_2), .eq(comparator_75_eq));  // open: gt, lt
  not not_13 (not_13_out, comparator_75_eq);
  not not_14 (not_14_out, comparator_76_eq);
  Comparator #(.width(5), .mode("unsigned")) comparator_76 (
    .a(5'b00111), .b(Read_Register_1), .eq(comparator_76_eq));  // open: gt, lt
  Comparator #(.width(5), .mode("unsigned")) comparator_77 (
    .a(5'b01000), .b(Read_Register_2), .eq(comparator_77_eq));  // open: gt, lt
  Comparator #(.width(5), .mode("unsigned")) comparator_78 (
    .a(5'b01000), .b(Read_Register_1), .eq(comparator_78_eq));  // open: gt, lt
  Comparator #(.width(5), .mode("unsigned")) comparator_79 (
    .a(5'b01001), .b(Read_Register_2), .eq(comparator_79_eq));  // open: gt, lt
  Comparator #(.width(5), .mode("unsigned")) comparator_80 (
    .a(5'b01001), .b(Read_Register_1), .eq(comparator_80_eq));  // open: gt, lt
  Comparator #(.width(5), .mode("unsigned")) comparator_81 (
    .a(5'b01011), .b(Read_Register_2), .eq(comparator_81_eq));  // open: gt, lt
  Comparator #(.width(5), .mode("unsigned")) comparator_82 (
    .a(5'b01011), .b(Read_Register_1), .eq(comparator_82_eq));  // open: gt, lt
  Comparator #(.width(5), .mode("unsigned")) comparator_83 (
    .a(5'b10001), .b(Read_Register_2), .eq(comparator_83_eq));  // open: gt, lt
  Comparator #(.width(5), .mode("unsigned")) comparator_84 (
    .a(5'b10001), .b(Read_Register_1), .eq(comparator_84_eq));  // open: gt, lt
  Comparator #(.width(5), .mode("unsigned")) comparator_85 (
    .a(5'b10011), .b(Read_Register_2), .eq(comparator_85_eq));  // open: gt, lt
  Comparator #(.width(5), .mode("unsigned")) comparator_86 (
    .a(5'b10011), .b(Read_Register_1), .eq(comparator_86_eq));  // open: gt, lt
  Comparator #(.width(5), .mode("unsigned")) comparator_87 (
    .a(5'b10101), .b(Read_Register_2), .eq(comparator_87_eq));  // open: gt, lt
  Comparator #(.width(5), .mode("unsigned")) comparator_88 (
    .a(5'b10101), .b(Read_Register_1), .eq(comparator_88_eq));  // open: gt, lt
  Register #(.width(32)) register_26 (.D(Write_Data), .en(and_26_out), .Q(register_26_q), .clk(Clock));  // open: clr
  Register #(.width(32)) register_27 (.D(Write_Data), .en(and_27_out), .Q(register_27_q), .clk(Clock));  // open: clr
  Register #(.width(32)) register_28 (.D(Write_Data), .en(and_28_out), .Q(register_28_q), .clk(Clock));  // open: clr
  Register #(.width(32)) register_29 (.D(Write_Data), .en(and_29_out), .Q(sp_Value), .clk(Clock));  // open: clr
  Register #(.width(32)) register_30 (.D(Write_Data), .en(and_30_out), .Q(register_30_q), .clk(Clock));  // open: clr
  Register #(.width(32)) register_31 (.D(Write_Data), .en(and_31_out), .Q(ra_Value), .clk(Clock));  // open: clr
  Register #(.width(32)) register_32 (.D(Write_Data), .en(1'b0), .Q(register_32_q), .clk(Clock));  // open: clr
  Transistor #(.width(32)) transistor_4 (.in(register_1_q), .out(Read_Data_1), .gate(not_2_out));
  Transistor #(.width(32)) transistor_5 (.in(register_2_q), .out(Read_Data_2), .gate(not_3_out));
  Transistor #(.width(32)) transistor_6 (.in(register_2_q), .out(Read_Data_1), .gate(not_4_out));
  Transistor #(.width(32)) transistor_7 (.in(register_3_q), .out(Read_Data_1), .gate(not_6_out));
  Transistor #(.width(32)) transistor_8 (.in(register_4_q), .out(Read_Data_2), .gate(not_7_out));
  Transistor #(.width(32)) transistor_9 (.in(register_4_q), .out(Read_Data_1), .gate(not_8_out));
  Transistor #(.width(32)) transistor_10 (.in(register_5_q), .out(Read_Data_1), .gate(not_10_out));
  Transistor #(.width(32)) transistor_11 (.in(register_6_q), .out(Read_Data_2), .gate(not_11_out));
  Transistor #(.width(32)) transistor_12 (.in(register_6_q), .out(Read_Data_1), .gate(not_12_out));
  Transistor #(.width(32)) transistor_13 (.in(register_7_q), .out(Read_Data_2), .gate(not_13_out));
  Transistor #(.width(32)) transistor_14 (.in(register_7_q), .out(Read_Data_1), .gate(not_14_out));
  not not_15 (not_15_out, comparator_77_eq);
  Transistor #(.width(32)) transistor_15 (.in(register_8_q), .out(Read_Data_2), .gate(not_15_out));
  not not_16 (not_16_out, comparator_78_eq);
  Transistor #(.width(32)) transistor_16 (.in(register_8_q), .out(Read_Data_1), .gate(not_16_out));
  not not_17 (not_17_out, comparator_79_eq);
  Transistor #(.width(32)) transistor_17 (.in(register_10_q), .out(Read_Data_2), .gate(not_17_out));
  not not_18 (not_18_out, comparator_80_eq);
  not not_19 (not_19_out, comparator_89_eq);
  Comparator #(.width(5), .mode("unsigned")) comparator_89 (
    .a(5'b01010), .b(Read_Register_2), .eq(comparator_89_eq));  // open: gt, lt
  Comparator #(.width(5), .mode("unsigned")) comparator_90 (
    .a(5'b01010), .b(Read_Register_1), .eq(comparator_90_eq));  // open: gt, lt
  not not_20 (not_20_out, comparator_90_eq);
  not not_21 (not_21_out, comparator_81_eq);
  Transistor #(.width(32)) transistor_18 (.in(register_12_q), .out(Read_Data_2), .gate(not_21_out));
  not not_22 (not_22_out, comparator_82_eq);
  Comparator #(.width(5), .mode("unsigned")) comparator_91 (
    .a(5'b01100), .b(Read_Register_2), .eq(comparator_91_eq));  // open: gt, lt
  not not_23 (not_23_out, comparator_91_eq);
  not not_24 (not_24_out, comparator_92_eq);
  Comparator #(.width(5), .mode("unsigned")) comparator_92 (
    .a(5'b01100), .b(Read_Register_1), .eq(comparator_92_eq));  // open: gt, lt
  not not_25 (not_25_out, comparator_93_eq);
  Comparator #(.width(5), .mode("unsigned")) comparator_93 (
    .a(5'b01101), .b(Read_Register_2), .eq(comparator_93_eq));  // open: gt, lt
  Transistor #(.width(32)) transistor_19 (.in(register_14_q), .out(Read_Data_2), .gate(not_25_out));
  Comparator #(.width(5), .mode("unsigned")) comparator_94 (
    .a(5'b01101), .b(Read_Register_1), .eq(comparator_94_eq));  // open: gt, lt
  not not_26 (not_26_out, comparator_94_eq);
  not not_27 (not_27_out, comparator_95_eq);
  Comparator #(.width(5), .mode("unsigned")) comparator_95 (
    .a(5'b01110), .b(Read_Register_2), .eq(comparator_95_eq));  // open: gt, lt
  Comparator #(.width(5), .mode("unsigned")) comparator_96 (
    .a(5'b01110), .b(Read_Register_1), .eq(comparator_96_eq));  // open: gt, lt
  not not_28 (not_28_out, comparator_96_eq);
  Comparator #(.width(5), .mode("unsigned")) comparator_97 (
    .a(5'b01111), .b(Read_Register_2), .eq(comparator_97_eq));  // open: gt, lt
  not not_29 (not_29_out, comparator_97_eq);
  not not_30 (not_30_out, comparator_98_eq);
  Comparator #(.width(5), .mode("unsigned")) comparator_98 (
    .a(5'b01111), .b(Read_Register_1), .eq(comparator_98_eq));  // open: gt, lt
  Comparator #(.width(5), .mode("unsigned")) comparator_99 (
    .a(5'b10000), .b(Read_Register_2), .eq(comparator_99_eq));  // open: gt, lt
  Comparator #(.width(5), .mode("unsigned")) comparator_100 (
    .a(5'b10000), .b(Read_Register_1), .eq(comparator_100_eq));  // open: gt, lt
  not not_31 (not_31_out, comparator_83_eq);
  Transistor #(.width(32)) transistor_20 (.in(s1_Value), .out(Read_Data_2), .gate(not_31_out));
  not not_32 (not_32_out, comparator_84_eq);
  Transistor #(.width(32)) transistor_21 (.in(s1_Value), .out(Read_Data_1), .gate(not_32_out));
  not not_33 (not_33_out, comparator_101_eq);
  Comparator #(.width(5), .mode("unsigned")) comparator_101 (
    .a(5'b10010), .b(Read_Register_2), .eq(comparator_101_eq));  // open: gt, lt
  Transistor #(.width(32)) transistor_22 (.in(s2_Value), .out(Read_Data_2), .gate(not_33_out));
  Comparator #(.width(5), .mode("unsigned")) comparator_102 (
    .a(5'b10010), .b(Read_Register_1), .eq(comparator_102_eq));  // open: gt, lt
  not not_34 (not_34_out, comparator_102_eq);
  not not_35 (not_35_out, comparator_85_eq);
  Transistor #(.width(32)) transistor_23 (.in(register_19_q), .out(Read_Data_2), .gate(not_35_out));
  not not_36 (not_36_out, comparator_86_eq);
  Comparator #(.width(5), .mode("unsigned")) comparator_103 (
    .a(5'b10100), .b(Read_Register_2), .eq(comparator_103_eq));  // open: gt, lt
  not not_37 (not_37_out, comparator_103_eq);
  Comparator #(.width(5), .mode("unsigned")) comparator_104 (
    .a(5'b10100), .b(Read_Register_1), .eq(comparator_104_eq));  // open: gt, lt
  not not_38 (not_38_out, comparator_104_eq);
  not not_39 (not_39_out, comparator_87_eq);
  Transistor #(.width(32)) transistor_24 (.in(register_21_q), .out(Read_Data_2), .gate(not_39_out));
  not not_40 (not_40_out, comparator_88_eq);
  not not_41 (not_41_out, comparator_105_eq);
  Comparator #(.width(5), .mode("unsigned")) comparator_105 (
    .a(5'b10110), .b(Read_Register_2), .eq(comparator_105_eq));  // open: gt, lt
  Comparator #(.width(5), .mode("unsigned")) comparator_106 (
    .a(5'b10110), .b(Read_Register_1), .eq(comparator_106_eq));  // open: gt, lt
  not not_42 (not_42_out, comparator_106_eq);
  Comparator #(.width(5), .mode("unsigned")) comparator_107 (
    .a(5'b10111), .b(Read_Register_2), .eq(comparator_107_eq));  // open: gt, lt
  not not_43 (not_43_out, comparator_107_eq);
  Transistor #(.width(32)) transistor_25 (.in(register_23_q), .out(Read_Data_2), .gate(not_43_out));
  not not_44 (not_44_out, comparator_108_eq);
  Comparator #(.width(5)) comparator_108 (.a(5'b10111), .b(Read_Register_1), .eq(comparator_108_eq));  // open: gt, lt
  Comparator #(.width(5)) comparator_109 (.a(5'b11000), .b(Read_Register_2), .eq(comparator_109_eq));  // open: gt, lt
  not not_45 (not_45_out, comparator_109_eq);
  not not_46 (not_46_out, comparator_110_eq);
  Comparator #(.width(5)) comparator_110 (.a(5'b11000), .b(Read_Register_1), .eq(comparator_110_eq));  // open: gt, lt
  Comparator #(.width(5)) comparator_111 (.a(5'b11001), .b(Read_Register_2), .eq(comparator_111_eq));  // open: gt, lt
  Comparator #(.width(5)) comparator_112 (.a(5'b11001), .b(Read_Register_1), .eq(comparator_112_eq));  // open: gt, lt
  Comparator #(.width(5)) comparator_113 (.a(5'b11011), .b(Read_Register_2), .eq(comparator_113_eq));  // open: gt, lt
  Comparator #(.width(5)) comparator_114 (.a(5'b11011), .b(Read_Register_1), .eq(comparator_114_eq));  // open: gt, lt
  Comparator #(.width(5)) comparator_115 (.a(5'b11101), .b(Read_Register_2), .eq(comparator_115_eq));  // open: gt, lt
  Comparator #(.width(5)) comparator_116 (.a(5'b11101), .b(Read_Register_1), .eq(comparator_116_eq));  // open: gt, lt
  Transistor #(.width(32)) transistor_26 (.in(register_10_q), .out(Read_Data_1), .gate(not_18_out));
  Transistor #(.width(32)) transistor_27 (.in(register_11_q), .out(Read_Data_2), .gate(not_19_out));
  Transistor #(.width(32)) transistor_28 (.in(register_11_q), .out(Read_Data_1), .gate(not_20_out));
  Transistor #(.width(32)) transistor_29 (.in(register_12_q), .out(Read_Data_1), .gate(not_22_out));
  Transistor #(.width(32)) transistor_30 (.in(register_13_q), .out(Read_Data_2), .gate(not_23_out));
  Transistor #(.width(32)) transistor_31 (.in(register_13_q), .out(Read_Data_1), .gate(not_24_out));
  Transistor #(.width(32)) transistor_32 (.in(register_14_q), .out(Read_Data_1), .gate(not_26_out));
  Transistor #(.width(32)) transistor_33 (.in(register_15_q), .out(Read_Data_2), .gate(not_27_out));
  Transistor #(.width(32)) transistor_34 (.in(register_15_q), .out(Read_Data_1), .gate(not_28_out));
  Transistor #(.width(32)) transistor_35 (.in(register_16_q), .out(Read_Data_2), .gate(not_29_out));
  Transistor #(.width(32)) transistor_36 (.in(register_16_q), .out(Read_Data_1), .gate(not_30_out));
  not not_47 (not_47_out, comparator_99_eq);
  Transistor #(.width(32)) transistor_37 (.in(s0_Value), .out(Read_Data_2), .gate(not_47_out));
  not not_48 (not_48_out, comparator_100_eq);
  Transistor #(.width(32)) transistor_38 (.in(s0_Value), .out(Read_Data_1), .gate(not_48_out));
  Transistor #(.width(32)) transistor_39 (.in(s2_Value), .out(Read_Data_1), .gate(not_34_out));
  Transistor #(.width(32)) transistor_40 (.in(register_19_q), .out(Read_Data_1), .gate(not_36_out));
  Transistor #(.width(32)) transistor_41 (.in(register_20_q), .out(Read_Data_2), .gate(not_37_out));
  Transistor #(.width(32)) transistor_42 (.in(register_20_q), .out(Read_Data_1), .gate(not_38_out));
  Transistor #(.width(32)) transistor_43 (.in(register_21_q), .out(Read_Data_1), .gate(not_40_out));
  Transistor #(.width(32)) transistor_44 (.in(register_22_q), .out(Read_Data_2), .gate(not_41_out));
  Transistor #(.width(32)) transistor_45 (.in(register_22_q), .out(Read_Data_1), .gate(not_42_out));
  Transistor #(.width(32)) transistor_46 (.in(register_23_q), .out(Read_Data_1), .gate(not_44_out));
  Transistor #(.width(32)) transistor_47 (.in(register_24_q), .out(Read_Data_2), .gate(not_45_out));
  Transistor #(.width(32)) transistor_48 (.in(register_24_q), .out(Read_Data_1), .gate(not_46_out));
  not not_49 (not_49_out, comparator_111_eq);
  Transistor #(.width(32)) transistor_49 (.in(register_25_q), .out(Read_Data_2), .gate(not_49_out));
  not not_50 (not_50_out, comparator_112_eq);
  Transistor #(.width(32)) transistor_50 (.in(register_25_q), .out(Read_Data_1), .gate(not_50_out));
  not not_51 (not_51_out, comparator_117_eq);
  Comparator #(.width(5)) comparator_117 (.a(5'b11010), .b(Read_Register_2), .eq(comparator_117_eq));  // open: gt, lt
  Transistor #(.width(32)) transistor_51 (.in(register_26_q), .out(Read_Data_2), .gate(not_51_out));
  not not_52 (not_52_out, comparator_118_eq);
  Comparator #(.width(5)) comparator_118 (.a(5'b11010), .b(Read_Register_1), .eq(comparator_118_eq));  // open: gt, lt
  not not_53 (not_53_out, comparator_113_eq);
  Transistor #(.width(32)) transistor_52 (.in(register_27_q), .out(Read_Data_2), .gate(not_53_out));
  not not_54 (not_54_out, comparator_114_eq);
  not not_55 (not_55_out, comparator_119_eq);
  Comparator #(.width(5)) comparator_119 (.a(5'b11100), .b(Read_Register_2), .eq(comparator_119_eq));  // open: gt, lt
  Comparator #(.width(5)) comparator_120 (.a(5'b11100), .b(Read_Register_1), .eq(comparator_120_eq));  // open: gt, lt
  not not_56 (not_56_out, comparator_120_eq);
  not not_57 (not_57_out, comparator_115_eq);
  Transistor #(.width(32)) transistor_53 (.in(sp_Value), .out(Read_Data_2), .gate(not_57_out));
  not not_58 (not_58_out, comparator_116_eq);
  Comparator #(.width(5)) comparator_121 (.a(5'b11110), .b(Read_Register_2), .eq(comparator_121_eq));  // open: gt, lt
  not not_59 (not_59_out, comparator_121_eq);
  Comparator #(.width(5)) comparator_122 (.a(5'b11110), .b(Read_Register_1), .eq(comparator_122_eq));  // open: gt, lt
  not not_60 (not_60_out, comparator_122_eq);
  Comparator #(.width(5)) comparator_123 (.a({5{1'b1}}), .b(Read_Register_2), .eq(comparator_123_eq));  // open: gt, lt
  not not_61 (not_61_out, comparator_123_eq);
  Transistor #(.width(32)) transistor_54 (.in(ra_Value), .out(Read_Data_2), .gate(not_61_out));
  Comparator #(.width(5)) comparator_124 (.a({5{1'b1}}), .b(Read_Register_1), .eq(comparator_124_eq));  // open: gt, lt
  not not_62 (not_62_out, comparator_124_eq);
  not not_63 (not_63_out, comparator_125_eq);
  Comparator #(.width(5)) comparator_125 (.a({5{1'b0}}), .b(Read_Register_2), .eq(comparator_125_eq));  // open: gt, lt
  not not_64 (not_64_out, comparator_126_eq);
  Comparator #(.width(5)) comparator_126 (.a({5{1'b0}}), .b(Read_Register_1), .eq(comparator_126_eq));  // open: gt, lt
  Transistor #(.width(32)) transistor_55 (.in(register_26_q), .out(Read_Data_1), .gate(not_52_out));
  Transistor #(.width(32)) transistor_56 (.in(register_27_q), .out(Read_Data_1), .gate(not_54_out));
  Transistor #(.width(32)) transistor_57 (.in(register_28_q), .out(Read_Data_2), .gate(not_55_out));
  Transistor #(.width(32)) transistor_58 (.in(register_28_q), .out(Read_Data_1), .gate(not_56_out));
  Transistor #(.width(32)) transistor_59 (.in(sp_Value), .out(Read_Data_1), .gate(not_58_out));
  Transistor #(.width(32)) transistor_60 (.in(register_30_q), .out(Read_Data_2), .gate(not_59_out));
  Transistor #(.width(32)) transistor_61 (.in(register_30_q), .out(Read_Data_1), .gate(not_60_out));
  Transistor #(.width(32)) transistor_62 (.in(ra_Value), .out(Read_Data_1), .gate(not_62_out));
  Transistor #(.width(32)) transistor_63 (.in(register_32_q), .out(Read_Data_2), .gate(not_63_out));
  Transistor #(.width(32)) transistor_64 (.in(register_32_q), .out(Read_Data_1), .gate(not_64_out));

  // Other names for the same wires on the sheet: clk = Clock; ra[31:0] = ra_Value; read_data1[31:0] = Read_Data_1;
  //   read_data2[31:0] = Read_Data_2; read_reg1[4:0] = Read_Register_1; read_reg2[4:0] = Read_Register_2;
  //   s0[31:0] = s0_Value; s1[31:0] = s1_Value; s2[31:0] = s2_Value; sp[31:0] = sp_Value; write_en = Write_Enable;
  //   write_reg[4:0] = Write_Register

  // Notes on the sheet:
  //   INPUTS to your circuit
  //   DON'T CHANGE THE LOCATIONS OF THE INPUTS AND OUTPUTS!
  //   These are DEBUG/TEST outputs from your circuit.
  //   OUTPUTS from your circuit
endmodule
